// Digital circuit HB Sound Control Build Logic Simulation V4.dig as structural Verilog
module HB_Sound_Control_Build_Logic_Simulation_V4 (
  input  RnW,
  input  nSE,
  input  [7:0] BUS_Write,
  input  E,
  input  A0,
  input  DIR_FIFO1,
  input  DIR_FIFO0,
  input  DOR_FIFO1,
  input  DOR_FIFO0,
  output [7:0] BUS_Read,
  output [1:0] Control__C0_C1,
  output [7:0] TO_FIFO,
  output SI_FIFO,
  output FIFO_RST,
  output E_B,
  output nSO_FIFO,
  output nOE_FIFO,
  output [7:0] COUNTER,
  output nRC
);

  wire A0_B, E_B_t, Flags_Ltch___U9_pin5, Flags_Ltch___U9_pin9, nand_4_out, nDIR, nDOR, not_3_out, not_4_out,
       nR_W, nRST, nSO_FIFO_B, R_nW_B, RCO;
  wire [7:0] BUS_IN;

  // ScopeTrigger scopetrigger_1: pin names not known; wires that end beside it: E
  assign BUS_IN = ~RnW ? BUS_Write : 8'bz;  // DriverInvSel driverinvsel_1
  _74161 Count_High___U2 (
    .pin1(nRST), .pin2(E), .pin3(1'b0), .pin4(1'b0), .pin5(1'b0), .pin6(1'b0), .pin7(RCO), .pin8(1'b0),
    .pin9(nRC), .pin10(1'b1), .pin11(COUNTER[7]), .pin12(COUNTER[6]), .pin13(COUNTER[5]), .pin14(COUNTER[4]),
    .pin16(1'b1));  // open: pin15
  Reset reset_1 (.out(nRST));
  not not_1 (FIFO_RST, nRST);
  not not_2 (nR_W, R_nW_B);
  EEPROM #(.AddrBits(10)) EEPROM (.A({Control__C0_C1, COUNTER}), .CS(1'b1), .WE(1'b0), .OE(1'b1), .D(nRC));
  _74161 Count_Low___U1 (
    .pin1(nRST), .pin2(E), .pin3(1'b0), .pin4(1'b0), .pin5(1'b0), .pin6(1'b0), .pin7(1'b1), .pin8(1'b0),
    .pin9(nRC), .pin10(1'b1), .pin11(COUNTER[3]), .pin12(COUNTER[2]), .pin13(COUNTER[1]), .pin14(COUNTER[0]),
    .pin15(RCO), .pin16(1'b1));
  not not_3 (not_3_out, nRC);
  not not_4 (not_4_out, E);
  nand nand_1 (nSO_FIFO_B, not_3_out, not_4_out);
  nand nand_2 (nDOR, DOR_FIFO1, DOR_FIFO0);
  nand nand_3 (nDIR, DIR_FIFO1, DIR_FIFO0);
  nand nand_4 (nand_4_out, E_B_t, nR_W);
  PullDown pulldown_1 (.out(TO_FIFO[0]));
  PullDown pulldown_2 (.out(TO_FIFO[1]));
  PullDown pulldown_3 (.out(TO_FIFO[2]));
  PullDown pulldown_4 (.out(TO_FIFO[3]));
  PullDown pulldown_5 (.out(TO_FIFO[4]));
  PullDown pulldown_6 (.out(TO_FIFO[5]));
  PullDown pulldown_7 (.out(TO_FIFO[6]));
  PullDown pulldown_8 (.out(TO_FIFO[7]));
  not not_5 (E_B, nand_4_out);
  _74194 Cnt__Reg____U8 (
    .pin1(nRST), .pin2(1'b0), .pin3(TO_FIFO[0]), .pin4(TO_FIFO[1]), .pin5(TO_FIFO[2]), .pin6(1'b0),
    .pin7(1'b0), .pin8(1'b0), .pin9(A0_B), .pin10(A0_B), .pin11(E_B), .pin13(nOE_FIFO),
    .pin14(Control__C0_C1[1]), .pin15(Control__C0_C1[0]), .pin16(1'b1));  // open: pin12
  PullDown pulldown_9 (.out(E_B_t));
  PullUp pullup_1 (.out(R_nW_B));
  PullDown pulldown_10 (.out(A0_B));
  _74245 Cnt__Bus__HCT____U6 (
    .pin1(1'b0), .pin2(R_nW_B), .pin3(A0_B), .pin4(E_B_t), .pin10(1'b0), .pin16(E), .pin17(A0), .pin18(RnW),
    .pin19(nSE), .pin20(1'b1));  // open: pin5, pin6, pin7, pin8, pin9, pin11, pin12, pin13, pin14, pin15
  _7474 Flags_Ltch___U9 (
    .pin1(nRST), .pin2(nDOR), .pin3(E), .pin4(1'b1), .pin5(Flags_Ltch___U9_pin5), .pin7(1'b0),
    .pin9(Flags_Ltch___U9_pin9), .pin10(1'b1), .pin11(E), .pin12(nDIR), .pin13(nRST), .pin14(1'b1));  // open: pin6, pin8
  _74125 Flags_Buff____U10 (
    .pin1(nR_W), .pin2(Flags_Ltch___U9_pin5), .pin3(TO_FIFO[0]), .pin4(nR_W), .pin5(Flags_Ltch___U9_pin9),
    .pin6(TO_FIFO[1]), .pin7(1'b0), .pin8(nSO_FIFO), .pin9(nSO_FIFO_B), .pin10(nOE_FIFO), .pin11(SI_FIFO),
    .pin12(E_B), .pin13(A0_B), .pin14(1'b1));
  PullUp pullup_2 (.out(BUS_IN[7]));
  PullUp pullup_3 (.out(BUS_IN[6]));
  PullUp pullup_4 (.out(BUS_IN[5]));
  PullUp pullup_5 (.out(BUS_IN[4]));
  PullUp pullup_6 (.out(BUS_IN[3]));
  PullUp pullup_7 (.out(BUS_IN[2]));
  PullUp pullup_8 (.out(BUS_IN[1]));
  PullUp pullup_9 (.out(BUS_IN[0]));
  _74245 Data_Bus__HCT__U7 (
    .pin1(R_nW_B), .pin2(TO_FIFO[0]), .pin3(TO_FIFO[1]), .pin4(TO_FIFO[2]), .pin5(TO_FIFO[3]),
    .pin6(TO_FIFO[4]), .pin7(TO_FIFO[5]), .pin8(TO_FIFO[6]), .pin9(TO_FIFO[7]), .pin10(1'b0),
    .pin11(BUS_IN[7]), .pin12(BUS_IN[6]), .pin13(BUS_IN[5]), .pin14(BUS_IN[4]), .pin15(BUS_IN[3]),
    .pin16(BUS_IN[2]), .pin17(BUS_IN[1]), .pin18(BUS_IN[0]), .pin19(nSE), .pin20(1'b1));
  PullDown pulldown_11 (.out(SI_FIFO));
  PullDown pulldown_12 (.out(E_B));
  assign BUS_Read = RnW ? BUS_IN : 8'bz;  // Driver driver_1
  PullDown #(.Bits(8)) pulldown_13 (.out(BUS_Read));

  // Other names for the same wires on the sheet: HB[3:0] = COUNTER[7:4]; Cl[3:0] = COUNTER[3:0];
  //   FIFO_INPUT[7:0] = TO_FIFO; CNT[1:0] = Control__C0_C1; BUS_OUT[7:0] = BUS_IN; DIR0 = DIR_FIFO0; DIR1 = DIR_FIFO1;
  //   DOR0 = DOR_FIFO0; DOR1 = DOR_FIFO1; RST = FIFO_RST; Write = E_B

  // Notes on the sheet:
  //   nSE: default 1
  //   E: Hz: 5
  //   U4 - 7414
  //   U5 - 7400
  //   U4 - 3
  //   U4 - 4
  //   HBSound Test Simulation V4
  //   U4 - 1,2
  //   contents of EEPROM (hex, n*v repeats v):
  //   56*1,0,313*1,0,370*1,0,281*1
  //   U5 - 1
  //   U5 - 2
  //   U5 - 3
  //   U5 - 4
  //   U4 - 5
endmodule
