// Digital circuit HBSound Count ROM Gate by Gate Logic.dig as structural Verilog
module HBSound_Count_ROM_Gate_by_Gate_Logic (
  input  C1,
  input  C0,
  input  A7,
  input  A6,
  input  A5,
  input  A4,
  input  A3,
  input  A2,
  input  A1,
  input  A0,
  output nRC
);

  wire and_1_out, and_2_out, and_3_out, and_4_out, and_5_out, and_6_out, and_7_out, and_8_out, and_9_out,
       and_10_out, and_11_out, and_12_out, and_13_out, and_14_out, and_15_out, and_16_out, and_17_out,
       and_18_out, not_1_out, not_2_out, not_3_out, not_4_out, not_5_out, not_6_out, not_7_out, not_8_out,
       not_9_out, not_10_out, or_1_out, or_2_out, or_3_out, or_4_out, or_5_out, or_6_out, or_7_out, or_8_out,
       or_9_out, or_10_out, or_11_out, or_12_out, or_13_out, or_14_out;

  not not_1 (not_1_out, C1);
  not not_2 (not_2_out, C0);
  not not_3 (not_3_out, A7);
  not not_4 (not_4_out, A6);
  not not_5 (not_5_out, A5);
  not not_6 (not_6_out, A4);
  not not_7 (not_7_out, A3);
  not not_8 (not_8_out, A2);
  not not_9 (not_9_out, A1);
  not not_10 (not_10_out, A0);
  and and_1 (and_1_out, A0, not_8_out);
  and and_2 (and_2_out, not_10_out, A2);
  and and_3 (and_3_out, A0, not_3_out);
  and and_4 (and_4_out, not_10_out, A7);
  and and_5 (and_5_out, A0, not_1_out);
  and and_6 (and_6_out, not_10_out, C1);
  and and_7 (and_7_out, not_10_out, not_6_out);
  and and_8 (and_8_out, A0, not_4_out);
  and and_9 (and_9_out, A0, A1);
  and and_10 (and_10_out, not_10_out, A1);
  and and_11 (and_11_out, A1, not_2_out);
  and and_12 (and_12_out, not_9_out, C0);
  and and_13 (and_13_out, not_9_out, A4);
  and and_14 (and_14_out, A3, not_6_out);
  and and_15 (and_15_out, not_7_out, not_4_out);
  or or_1 (or_1_out, and_1_out, and_2_out);
  or or_2 (or_2_out, and_3_out, and_4_out);
  or or_3 (or_3_out, and_5_out, and_6_out);
  or or_4 (or_4_out, and_7_out, and_8_out);
  and and_16 (and_16_out, and_9_out, not_7_out);
  and and_17 (and_17_out, and_10_out, A3);
  or or_5 (or_5_out, and_11_out, and_12_out);
  and and_18 (and_18_out, and_13_out, A6);
  or or_6 (or_6_out, and_15_out, not_5_out);
  or or_7 (or_7_out, or_1_out, or_2_out);
  or or_8 (or_8_out, or_3_out, or_4_out);
  or or_9 (or_9_out, and_16_out, and_17_out);
  or or_10 (or_10_out, and_18_out, and_14_out);
  or or_11 (or_11_out, or_7_out, or_8_out);
  or or_12 (or_12_out, or_9_out, or_5_out);
  or or_13 (or_13_out, or_10_out, or_6_out);
  or or_14 (or_14_out, or_12_out, or_13_out);
  or or_15 (nRC, or_11_out, or_14_out);

  // Notes on the sheet:
  //   nRC: pin 14
  //   C1: pin 11
  //   C0: pin 10
  //   A7: pin 9
  //   A6: pin 8
  //   A5: pin 7
  //   A4: pin 6
  //   A3: pin 5
  //   A2: pin 4
  //   A1: pin 3
  //   A0: pin 2
endmodule
