// Digital circuit HBSound Count Rom Simplified Logic V2.dig as structural Verilog
module HBSound_Count_Rom_Simplified_Logic_V2 (
  input  C1,
  input  C0,
  input  CA7,
  input  CA6,
  input  CA5,
  input  CA4,
  input  CA3,
  input  CA2,
  input  CA1,
  input  CA0,
  input  nRST__C6,
  input  E__C5,
  input  R_nW__C4,
  input  A0__C3,
  input  SE__C2,
  output D0__RC,
  output D1__SO_FIFO,
  output D2__nCLK_R,
  output D3__nSI_FIFO,
  output D4__RST_SR,
  output D5__RST
);

  wire B00_eq, B01_eq, B10_eq, B11_eq, CLK_R, decoder_2_out_0, decoder_2_out_1, decoder_2_out_2,
       decoder_2_out_3, driver_1_out, nR_W, nRC, nRST_SR, pullup_1_out, SI_FIFO;
  wire [1:0] driverinvsel_2_out;

  not not_1 (nR_W, R_nW__C4);
  PullUp pullup_1 (.out(pullup_1_out));
  assign pullup_1_out = ~SE__C2 ? nR_W : 1'bz;  // DriverInvSel driverinvsel_1
  Decoder #(.Selector_Bits(2)) decoder_1 (.sel({nRC, E__C5}), .out_0(D1__SO_FIFO));  // open: out_1, out_2, out_3
  and and_1 (nRST_SR, pullup_1_out, nRST__C6);
  Decoder #(.Selector_Bits(2)) decoder_2 (
    .sel({C1, C0}), .out_0(decoder_2_out_0), .out_1(decoder_2_out_1), .out_2(decoder_2_out_2),
    .out_3(decoder_2_out_3));
  Comparator #(.Bits(8)) B00 (.a({CA7, CA6, CA5, CA4, CA3, CA2, CA1, CA0}), .b(8'h38), .eq(B00_eq));  // open: gt, lt
  Comparator #(.Bits(8)) B01 (.a({CA7, CA6, CA5, CA4, CA3, CA2, CA1, CA0}), .b(8'h72), .eq(B01_eq));  // open: gt, lt
  Comparator #(.Bits(8)) B10 (.a({CA7, CA6, CA5, CA4, CA3, CA2, CA1, CA0}), .b(8'he5), .eq(B10_eq));  // open: gt, lt
  Comparator #(.Bits(8)) B11 (
    .a({CA7, CA6, CA5, CA4, CA3, CA2, CA1, CA0}), .b({8{1'b1}}), .eq(B11_eq));  // open: gt, lt
  assign driver_1_out = decoder_2_out_0 ? B00_eq : 1'bz;  // Driver driver_1
  assign driver_1_out = decoder_2_out_1 ? B01_eq : 1'bz;  // Driver driver_2
  assign driverinvsel_2_out = ~SE__C2 ? {A0__C3, E__C5} : 2'bz;  // DriverInvSel driverinvsel_2
  PullDown #(.Bits(2)) pulldown_1 (.out(driverinvsel_2_out));
  assign driver_1_out = decoder_2_out_2 ? B10_eq : 1'bz;  // Driver driver_3
  Decoder #(.Selector_Bits(2)) decoder_3 (
    .sel(driverinvsel_2_out), .out_1(SI_FIFO), .out_3(CLK_R));  // open: out_0, out_2
  assign driver_1_out = decoder_2_out_3 ? B11_eq : 1'bz;  // Driver driver_4
  not not_2 (nRC, driver_1_out);
  not not_3 (D0__RC, nRC);
  not not_4 (D2__nCLK_R, CLK_R);
  not not_5 (D3__nSI_FIFO, SI_FIFO);
  not not_6 (D4__RST_SR, nRST_SR);

  assign D5__RST = nRST__C6;

  // Other names for the same wires on the sheet: A0 = A0__C3; E = E__C5; nRST = nRST__C6; nSE = SE__C2;
  //   nSO_FIFO = D1__SO_FIFO; R_nW = R_nW__C4

  // Notes on the sheet:
  //   nRST__C6: default 1
  //   SE__C2: default 1
  //   Counter Rom
endmodule
